// Digital circuit comparatorWithDecoders.dig as structural Verilog
module comparatorWithDecoders (
  input  B_1,
  input  B_0,
  input  A_1,
  input  A_0,
  input  [1:0] X,
  input  in_7,
  input  in_8,
  input  in_9,
  input  B_2,
  input  A_2,
  input  B_3,
  input  A_3,
  input  B_4,
  input  A_4,
  input  B_5,
  input  A_5,
  input  B_6,
  input  A_6,
  input  [1:0] in_21,
  input  in_22,
  input  in_23,
  input  in_24,
  input  in_25,
  input  in_26,
  input  in_27,
  input  in_28,
  input  in_29,
  input  in_30,
  input  in_31,
  input  in_32,
  input  in_33,
  input  in_34,
  input  in_35,
  output [1:0] out_6,
  output [1:0] out_12
);

  wire and_1_out, and_2_out, decoder_1_out_0, decoder_1_out_1, decoder_1_out_2, decoder_1_out_3,
       decoder_2_out_0, decoder_2_out_1, decoder_2_out_2, decoder_2_out_3, decoder_2_out_4, decoder_2_out_5,
       decoder_2_out_6, decoder_2_out_7, decoder_3_out_0, decoder_3_out_1, decoder_3_out_2, decoder_3_out_3,
       decoder_3_out_4, decoder_3_out_5, decoder_3_out_6, decoder_3_out_7, decoder_4_out_0, decoder_4_out_1,
       decoder_4_out_2, decoder_4_out_3, decoder_5_out_0, decoder_5_out_1, decoder_5_out_2, decoder_5_out_3,
       decoder_6_out_1, decoder_6_out_2, decoder_6_out_3, decoder_6_out_4, decoder_6_out_6, decoder_7_out_0,
       decoder_7_out_5, decoder_7_out_7, decoder_8_out_0, decoder_8_out_1, decoder_8_out_2, decoder_8_out_3,
       decoder_9_out_0, decoder_9_out_5, decoder_9_out_7, decoder_10_out_0, decoder_10_out_1,
       decoder_10_out_2, decoder_10_out_3, nor_1_out, not_1_out, not_2_out, or_1_out, or_2_out, or_3_out,
       or_4_out, or_5_out, xnor_1_out;

  Decoder #(.Selector_Bits(2)) decoder_1 (
    .sel(X), .out_0(decoder_1_out_0), .out_1(decoder_1_out_1), .out_2(decoder_1_out_2),
    .out_3(decoder_1_out_3));
  LED led_1 (.in(decoder_1_out_0));
  LED led_2 (.in(decoder_1_out_2));
  LED led_3 (.in(decoder_1_out_1));
  LED led_4 (.in(decoder_1_out_3));
  not not_1 (not_1_out, B_1);
  not not_2 (not_2_out, A_1);
  and and_1 (and_1_out, A_1, not_1_out);
  xnor xnor_1 (xnor_1_out, A_1, B_1);
  and and_2 (and_2_out, not_2_out, B_1);
  Decoder #(.Selector_Bits(3)) decoder_2 (
    .sel({in_26, in_25, in_24}), .out_0(decoder_2_out_0), .out_1(decoder_2_out_1), .out_2(decoder_2_out_2),
    .out_3(decoder_2_out_3), .out_4(decoder_2_out_4), .out_5(decoder_2_out_5), .out_6(decoder_2_out_6),
    .out_7(decoder_2_out_7));
  Decoder #(.Selector_Bits(3)) decoder_3 (
    .sel({in_22, in_21}), .out_0(decoder_3_out_0), .out_1(decoder_3_out_1), .out_2(decoder_3_out_2),
    .out_3(decoder_3_out_3), .out_4(decoder_3_out_4), .out_5(decoder_3_out_5), .out_6(decoder_3_out_6),
    .out_7(decoder_3_out_7));
  LED led_5 (.in(decoder_2_out_0));
  LED led_6 (.in(decoder_2_out_2));
  LED led_7 (.in(decoder_2_out_4));
  LED led_8 (.in(decoder_2_out_6));
  LED led_9 (.in(decoder_3_out_0));
  LED led_10 (.in(decoder_3_out_2));
  LED led_11 (.in(decoder_3_out_4));
  LED led_12 (.in(decoder_3_out_6));
  Decoder #(.Selector_Bits(2)) decoder_4 (
    .sel({B_3, A_3}), .out_0(decoder_4_out_0), .out_1(decoder_4_out_1), .out_2(decoder_4_out_2),
    .out_3(decoder_4_out_3));
  LED led_13 (.in(decoder_2_out_1));
  LED led_14 (.in(decoder_2_out_3));
  LED led_15 (.in(decoder_2_out_5));
  LED led_16 (.in(decoder_2_out_7));
  LED led_17 (.in(decoder_3_out_1));
  LED led_18 (.in(decoder_3_out_3));
  LED led_19 (.in(decoder_3_out_5));
  LED led_20 (.in(decoder_3_out_7));
  LED led_21 (.in(decoder_4_out_0));
  LED led_22 (.in(decoder_4_out_1));
  LED led_23 (.in(decoder_4_out_2));
  LED led_24 (.in(decoder_4_out_3));
  Decoder #(.Selector_Bits(2)) decoder_5 (
    .sel({B_4, A_4}), .out_0(decoder_5_out_0), .out_1(decoder_5_out_1), .out_2(decoder_5_out_2),
    .out_3(decoder_5_out_3));
  or or_1 (or_1_out, decoder_5_out_0, decoder_5_out_3);
  Decoder #(.Selector_Bits(3)) decoder_6 (
    .sel({in_29, in_28, in_27}), .out_1(decoder_6_out_1), .out_2(decoder_6_out_2), .out_3(decoder_6_out_3),
    .out_4(decoder_6_out_4), .out_6(decoder_6_out_6));  // open: out_0, out_5, out_7
  Decoder #(.Selector_Bits(3)) decoder_7 (
    .sel({in_32, in_31, in_30}), .out_0(decoder_7_out_0), .out_5(decoder_7_out_5), .out_7(decoder_7_out_7));  // open: out_1, out_2, out_3, out_4, out_6
  LED led_25 (.in(decoder_5_out_1));
  LED led_26 (.in(or_1_out));
  LED led_27 (.in(decoder_5_out_2));
  or or_2 (or_2_out, decoder_6_out_1, decoder_6_out_2, decoder_6_out_3, decoder_6_out_4, decoder_6_out_6);
  or or_3 (or_3_out, decoder_7_out_0, decoder_7_out_5, decoder_7_out_7);
  LED led_28 (.in(or_2_out));
  LED led_29 (.in(or_3_out));
  Decoder #(.Selector_Bits(2)) decoder_8 (
    .sel({B_5, A_5}), .out_0(decoder_8_out_0), .out_1(decoder_8_out_1), .out_2(decoder_8_out_2),
    .out_3(decoder_8_out_3));
  Decoder #(.Selector_Bits(3)) decoder_9 (
    .sel({in_35, in_34, in_33}), .out_0(decoder_9_out_0), .out_5(decoder_9_out_5), .out_7(decoder_9_out_7));  // open: out_1, out_2, out_3, out_4, out_6
  or or_4 (or_4_out, decoder_8_out_0, decoder_8_out_3);
  nor nor_1 (nor_1_out, decoder_9_out_0, decoder_9_out_5, decoder_9_out_7);
  LED led_30 (.in(nor_1_out));
  Decoder #(.Selector_Bits(2)) decoder_10 (
    .sel({B_6, A_6}), .out_0(decoder_10_out_0), .out_1(decoder_10_out_1), .out_2(decoder_10_out_2),
    .out_3(decoder_10_out_3));
  or or_5 (or_5_out, decoder_10_out_0, decoder_10_out_3);
  LED led_31 (.in(decoder_10_out_1));
  LED led_32 (.in(or_5_out));
  LED led_33 (.in(decoder_10_out_2));

  assign out_6 = {in_8, in_7};
  assign out_12 = {B_2, A_2};

  // Notes on the sheet:
  //   in_21: This control 2 bits
  //   A_1 A_0
  //   B1 B_0
  //   Compare
  //   A_1(B_1)' = 10 = 2
  //   A_1 B_1+(A_1)'(B_1)' = 00, 11 = 0, 3
  //   (A_1)'B = 01 = 1
  //   Comparator 1-Bit
  //   F(1,2,3,4,6,)
  //   F'(0,5,7)
  //   A>B
  //   A=B
  //   A<B
  //   [F'(0,5,7)]' = F
  //   Comparator 2-Bit
endmodule
