// Digital circuit deneme.dig as structural Verilog
module deneme (
  input  in_1,
  input  in_2
);

  wire u_and_gate_y;

  and_gate #(.applicationType("IVERILOG")) u_and_gate (.a(in_1), .b(in_2), .y(u_and_gate_y));
  LED led_1 (.in(u_and_gate_y));
endmodule

/* Code of and_gate:
module and_gate(a,b,y);
input a,b;
output y;
and(y,a,b);
endmodule
*/
